# Fritzing sketch Baseboard (saved by Fritzing 0.9.3b)
breadboards: 1

parts:
  元件1 = Arduino Mega 2560 (Rev3)
  J3 = Infrared Proximity Sensor
  J4 = Infrared Proximity Sensor
  J5 = Infrared Proximity Sensor
  J6 = Infrared Proximity Sensor
  M2 = DC Motor
  BTN7971 = L298 [package=multiwatt15]
  A_12V_Chargeable_Battery1 = Battery Holders [package=battery-aaa]
  M3 = DC Motor
  BTN7972 = L298 [package=multiwatt15]
  A_12V_Chargeable_Battery2 = Battery Holders [package=battery-aaa]
  M4 = DC Motor
  M5 = DC Motor
  A_5V_Charge_Pal1 = Battery Holders [package=battery-aaa]  # not connected
  J7 = Infrared Proximity Sensor
  元件2 = Compass Module - HMC6352 [part_number="Posture Sensor"]

nets:
  N1: 元件1.A0, J6.Vcc
  N2: 元件1.A1, J5.Vcc
  N3: 元件1.A2, J4.Vcc
  N4: 元件1.A3, J3.Vcc
  N5: 元件1.D19/RX1, 元件2.SCL
  N6: 元件1.D13_PWM, BTN7972.IN4
  N7: 元件1.D12_PWM, BTN7972.IN3
  N8: 元件1.D11_PWM, BTN7972.IN2
  N9: 元件1.D10_PWM, BTN7972.IN1
  N10: 元件1.D9_PWM, BTN7971.IN4
  N11: 元件1.D8_PWM, BTN7971.IN3
  5V: 元件1.5V, J3.Vout, J4.Vout, J5.Vout, J6.Vout, J7.Vout, 元件2.VCC
  GND: 元件1.GND, J3.GND, J4.GND, J5.GND, J6.GND, J7.GND, 元件2.GND
  N12: 元件1.D4_PWM, BTN7971.ENA
  N13: 元件1.D5_PWM, BTN7972.ENA
  N14: 元件1.D6_PWM, BTN7971.IN1
  N15: 元件1.D7_PWM, BTN7971.IN2
  N16: 元件1.D45, J7.Vcc
  N17: M2.pin_1, BTN7971.OUT4
  N18: M2.pin_2, BTN7971.OUT3
  N19: BTN7971.OUT1, M3.pin_2
  N20: BTN7971.OUT2, M3.pin_1
  N21: BTN7971.VS, A_12V_Chargeable_Battery1.+
  N22: BTN7971.GND, A_12V_Chargeable_Battery1.-
  N23: BTN7972.OUT1, M4.pin_2
  N24: BTN7972.OUT2, M4.pin_1
  N25: BTN7972.VS, A_12V_Chargeable_Battery2.+
  N26: BTN7972.GND, A_12V_Chargeable_Battery2.-
  N27: BTN7972.OUT3, M5.pin_2
  N28: BTN7972.OUT4, M5.pin_1
