# Fritzing sketch Circuit (saved by Fritzing 0.9.3b)

parts:
  元件1 = Arduino Mega 2560 (Rev3)
  L298N = L298 [package=multiwatt15]
  Right_Motor = DC Motor
  Left_Motor = DC Motor
  LED1 = RGB LED - (4 legs) [package="5 mm [THT]"]
  Head_Infrared_Sensor = Infrared Proximity Sensor
  Right_Infrared_Sensor = Infrared Proximity Sensor
  Right_Head_Infrared_Sensor = Infrared Proximity Sensor
  Left_Head_Infrared_Sensor = Infrared Proximity Sensor
  Left_Infrared_Sensor = Infrared Proximity Sensor
  A_5V_Charge_Pal = Battery Holders [package=battery-aaa]  # not connected
  A_12V_Chargeable_Battery = Battery Holders [package=battery-aaa]
  An_OpenMv_Camera = Arduino USB Host Shield

nets:
  N1: 元件1.D19/RX1, An_OpenMv_Camera.RX
  N2: 元件1.D18/TX1, An_OpenMv_Camera.TX
  N3: 元件1.D13_PWM, L298N.ENB
  N4: 元件1.D12_PWM, L298N.ENA
  N5: 元件1.D10_PWM, Left_Head_Infrared_Sensor.Vcc
  N6: 元件1.D9_PWM, Head_Infrared_Sensor.Vcc
  N7: 元件1.5V, Head_Infrared_Sensor.Vout, Right_Infrared_Sensor.Vout, Right_Head_Infrared_Sensor.Vout, Left_Head_Infrared_Sensor.Vout, Left_Infrared_Sensor.Vout, An_OpenMv_Camera.5V-ARDUINO
  GND: 元件1.GND, LED1.blue_cathode, Head_Infrared_Sensor.GND, Right_Infrared_Sensor.GND, Right_Head_Infrared_Sensor.GND, Left_Head_Infrared_Sensor.GND, Left_Infrared_Sensor.GND, An_OpenMv_Camera.GND
  N8: 元件1.D3_PWM, L298N.IN3
  N9: 元件1.D4_PWM, L298N.IN4
  N10: 元件1.D5_PWM, L298N.IN1
  N11: 元件1.D7_PWM, Right_Infrared_Sensor.Vcc
  N12: 元件1.D22, Right_Head_Infrared_Sensor.Vcc
  N13: 元件1.D44, Left_Infrared_Sensor.Vcc
  N14: 元件1.D46, LED1.red_cathode
  N15: 元件1.D48, LED1.green_cathode
  N16: L298N.OUT1, Right_Motor.pin_2
  N17: L298N.OUT2, Right_Motor.pin_1
  N18: L298N.VS, A_12V_Chargeable_Battery.+
  N19: L298N.GND, A_12V_Chargeable_Battery.-
  N20: L298N.OUT3, Left_Motor.pin_2
  N21: L298N.OUT4, Left_Motor.pin_1
