# Fritzing sketch Lift system (saved by Fritzing 0.9.3b)

parts:
  元件1 = Arduino Uno (Rev3) - ICSP
  L298N1 = L298 [package=multiwatt15]
  A_12V_Chargeable_Battery1 = Battery Holders [package=battery-aaa]
  Lift_Motor = DC Motor
  Pack_Motor = DC Motor
  Laser_Launcher_and_Receiver = Grove Infrared Receiver

nets:
  N1: 元件1.ICSP_MISO, 元件1.D12/MISO, Laser_Launcher_and_Receiver.RX
  N2: 元件1.D3_PWM, L298N1.IN1
  N3: 元件1.D4, L298N1.IN2
  N4: 元件1.D5_PWM, L298N1.IN3
  N5: 元件1.D6_PWM, L298N1.IN4
  N6: 元件1.D7, L298N1.ENB
  5V: 元件1.5V, Laser_Launcher_and_Receiver.VCC
  GND: 元件1.GND, Laser_Launcher_and_Receiver.GND
  N7: L298N1.OUT1, Lift_Motor.pin_2
  N8: L298N1.OUT2, Lift_Motor.pin_1
  N9: L298N1.VS, A_12V_Chargeable_Battery1.+
  N10: L298N1.GND, A_12V_Chargeable_Battery1.-
  N11: L298N1.OUT3, Pack_Motor.pin_2
  N12: L298N1.OUT4, Pack_Motor.pin_1
